# Fritzing sketch lab3 (saved by Fritzing 0.9.3b)
breadboards: 1

parts:
  41MUX_for_routing = IC, DIP package, 16 pins [chip_label=153]  # not connected
  21MUX = IC, DIP package, 16 pins [chip_label=157]
  NAND = IC, DIP package, 14 pins [chip_label=00]
  NOR = IC, DIP package, 14 pins [chip_label=02]
  XOR = IC, DIP package, 14 pins [chip_label=86]
  NOT = IC, DIP package, 14 pins [chip_label=04]
  SR-B = IC, DIP package, 16 pins [chip_label="194 SR"]
  SR-A = IC, DIP package, 16 pins [chip_label="194 SR"]
  41MUX_for_computation = IC, DIP package, 16 pins [chip_label=153]

nets:
  F'(A, B): 21MUX.pin13, NOT.pin9, 41MUX_for_computation.pin9
  F(A, B): 21MUX.pin14, NOT.pin8
  GND: 21MUX.pin15, 41MUX_for_computation.pin13, 41MUX_for_computation.pin15
  SR-A: NAND.pin4, NOR.pin4, XOR.pin4, SR-A.pin12
  SR-B: NAND.pin5, NOR.pin5, XOR.pin5, SR-B.pin12
  A NAND B: NAND.pin6, 41MUX_for_computation.pin10
  A NOR B: NOR.pin6, 41MUX_for_computation.pin11
  A XOR B: NOR.pin8, NOR.pin9, XOR.pin6
  A XNOR B: NOR.pin10, 41MUX_for_computation.pin12
  5V: SR-B.pin1, SR-A.pin1
  D3: SR-B.pin3, SR-A.pin3
  D2: SR-B.pin4, SR-A.pin4
  D1: SR-B.pin5, SR-A.pin5
  D0: SR-B.pin6, SR-A.pin6
  CLK: SR-B.pin11, SR-A.pin11
  F1: 41MUX_for_computation.pin2
  F0: 41MUX_for_computation.pin14
